# Fritzing sketch PetBot (saved by Fritzing 0.9.0b)
breadboards: 1

parts:
  Part1 = Arduino Uno (Rev3)
  S1 = Pushbutton [package="[THT]"]
  S2 = Pushbutton [package="[THT]"]
  R1 = Resistor [tolerance=±5% resistance=220 package=THT]
  R2 = Resistor [tolerance=±5% resistance=220 package=THT]
  J1 = Basic Servo
  C1 = Electrolytic Capacitor [capacitance=1µF package="100 mil [THT, electrolytic]"]
  M1 = DC Motor  # not connected
  R3 = Resistor [tolerance=±5% resistance=220 package=THT]
  R4 = Resistor [tolerance=±5% resistance=220 package=THT]
  Q1 = NPN-Transistor [package="TO92 [THT]"]
  Q2 = NPN-Transistor [package="TO92 [THT]"]
  VCC1 = Battery  # not connected
  U1 = mystery part, 3 pins [chip_label=?]
  U2 = mystery part, 3 pins [chip_label=?]  # not connected
  U3 = mystery part, 3 pins [chip_label=?]  # not connected
  VCC2 = Battery  # not connected
  U4 = 640x480 CMOS Color Camera [package=camera_cmos_con]  # not connected

nets:
  N1: Part1.D9_PWM, Q1.B
  N2: Part1.D10_PWM/SS, J1.pulse
  N3: Part1.D2, S1.Pin_1, S1.Pin_2, R1.Pin_0
  N4: Part1.D3_PWM, S2.Pin_3, S2.Pin_4, R2.Pin_0
  N5: Part1.3V3, C1.+, R3.Pin_0, R4.Pin_0
  N6: Part1.5V, R1.Pin_1, R2.Pin_1
  GND: Part1.GND, S1.Pin_3, S1.Pin_4, S2.Pin_1, S2.Pin_2, J1.gnd, C1.-, Q1.E, Q2.E, U1.pin3
  N7: J1.vcc, U1.pin2
  N8: R3.Pin_1, Q1.C, Q2.B
  N9: R4.Pin_1, Q2.C, U1.pin1
